# Fritzing sketch RTT (saved by Fritzing 0.9.3b)
breadboards: 1

parts:
  Bauteil1 = Arduino Uno (Rev3)
  R1 = Resistor [tolerance=±5% resistance=220 package=THT]
  R2 = Resistor [tolerance=±5% resistance=220 package=THT]
  LED_2_green = LED - 5mm [color="Green (555nm)" package="5 mm [THT]"]
  LED_1_red = LED - 5mm [color="Red (633nm)" package="5 mm [THT]"]
  Button_1 = Pushbutton [package="[THT]"]
  Button_2 = Pushbutton [package="[THT]"]

nets:
  N1: Bauteil1.D10_PWM/SS, R1.Pin_0
  N2: Bauteil1.D11_PWM/MOSI, R2.Pin_0
  N3: Bauteil1.D12/MISO, Button_2.Pin_1, Button_2.Pin_2
  N4: Bauteil1.D13/SCK, Button_1.Pin_1, Button_1.Pin_2
  N5: Bauteil1.GND, LED_2_green.cathode, LED_1_red.cathode, Button_1.Pin_3, Button_1.Pin_4, Button_2.Pin_3, Button_2.Pin_4
  N6: R1.Pin_1, LED_2_green.anode
  N7: R2.Pin_1, LED_1_red.anode
