# Fritzing sketch RTT_v2_LCD (saved by Fritzing 0.9.3b)
breadboards: 1

parts:
  Bauteil1 = Arduino Uno (Rev3)
  R1 = Resistor [tolerance=±5% resistance=220 package=THT]
  R2 = Resistor [tolerance=±5% resistance=220 package=THT]
  LED_2_green = LED - 5mm [color="Green (555nm)" package="5 mm [THT]"]
  LED_1_red = LED - 5mm [color="Red (633nm)" package="5 mm [THT]"]
  Button_1 = Pushbutton [package="[THT]"]
  Button_2 = Pushbutton [package="[THT]"]
  Display = LCD-16X2 [package=lcd-16x2]
  LCM1602_IIC2 = LCM1602 IIC [part_number="LCM1602 IIC" chip_label="LCM1602 IIC" package="DIP (Dual Inline) [THT]"]

nets:
  N1: Bauteil1.A4/SDA, LCM1602_IIC2.SDA
  N2: Bauteil1.A5/SCL, LCM1602_IIC2.SCL
  N3: Bauteil1.D10_PWM/SS, R1.Pin_0
  N4: Bauteil1.D11_PWM/MOSI, R2.Pin_0
  N5: Bauteil1.D12/MISO, Button_2.Pin_1, Button_2.Pin_2
  N6: Bauteil1.D13/SCK, Button_1.Pin_1, Button_1.Pin_2
  GND: Bauteil1.GND, LED_2_green.cathode, LED_1_red.cathode, Button_1.Pin_3, Button_1.Pin_4, Button_2.Pin_3, Button_2.Pin_4, LCM1602_IIC2.GND
  5V: Bauteil1.5V, LCM1602_IIC2.VCC, LCM1602_IIC2.LED_A
  N7: R1.Pin_1, LED_2_green.anode
  N8: R2.Pin_1, LED_1_red.anode
  VSS: Display.VSS, LCM1602_IIC2.VSS
  VDD: Display.VDD, LCM1602_IIC2.VDD
  N9: Display.VO, LCM1602_IIC2.V0
  N10: Display.RS, LCM1602_IIC2.RS
  N11: Display.R_W, LCM1602_IIC2.RW
  N12: Display.E, LCM1602_IIC2.E
  N13: Display.DB0, LCM1602_IIC2.D0
  N14: Display.DB1, LCM1602_IIC2.D1
  N15: Display.DB2, LCM1602_IIC2.D2
  N16: Display.DB3, LCM1602_IIC2.D3
  N17: Display.DB4, LCM1602_IIC2.D4
  N18: Display.DB5, LCM1602_IIC2.D5
  N19: Display.DB6, LCM1602_IIC2.D6
  N20: Display.DB7, LCM1602_IIC2.D7
  N21: Display.A, LCM1602_IIC2.A
  N22: Display.K, LCM1602_IIC2.K

custom parts:
  LCM1602 IIC: I2C-Module to use a 1602 or 2004 LCD on with the wire.h libory Serial LCD Modul
