# Fritzing sketch RTT_v3_4x7 (saved by Fritzing 0.9.3b)
breadboards: 1

parts:
  Button_2 = Pushbutton [package="[SMD]"]
  Button_1 = Pushbutton [package="[SMD]"]
  LED_1_red = smd LED [color="Red (633nm)" package="1206 [SMD]"]
  LED_2_green = smd LED [color="Green (555nm)" package="1206 [SMD]"]
  220_Ohm = Resistor [tolerance=±5% power=0.25 resistance=220 package=THT]
  R2 = Resistor [tolerance=±5% power=0.25 resistance=220 package=THT]
  Display = 7-SEGMENT-4DIGIT-YOUNGSUN [package=7-segment-4digit-youngsun]
  R3 = Resistor [tolerance=±5% resistance=1k package=THT]
  R4 = Resistor [tolerance=±5% resistance=1k package=THT]
  R5 = Resistor [tolerance=±5% resistance=1k package=THT]
  R6 = Resistor [tolerance=±5% resistance=1k package=THT]
  Bauteil1 = Arduino Uno (Rev3)

nets:
  N1: Button_2.Pin_1, Button_2.Pin_2, Bauteil1.D12/MISO
  N2: Button_2.Pin_3, Button_2.Pin_4, Button_1.Pin_3, Button_1.Pin_4, LED_1_red.cathode, LED_2_green.cathode, Bauteil1.GND
  N3: Button_1.Pin_1, Button_1.Pin_2, Bauteil1.D13/SCK
  N4: LED_1_red.anode, 220_Ohm.Pin_1
  N5: LED_2_green.anode, R2.Pin_1
  N6: 220_Ohm.Pin_0, Bauteil1.D11_PWM/MOSI
  N7: R2.Pin_0, Bauteil1.D10_PWM/SS
  N8: Display.DIG1, R3.Pin_0
  N9: Display.DIG2, R4.Pin_0
  N10: Display.D, Bauteil1.D5_PWM
  N11: Display.E, Bauteil1.D6_PWM
  N12: Display.DIG3, R6.Pin_0
  N13: Display.DP, Bauteil1.D9_PWM
  N14: Display.DIG4, R5.Pin_0
  N15: Display.F, Bauteil1.D7
  N16: Display.C, Bauteil1.D4
  N17: Display.A, Bauteil1.D2
  N18: Display.G, Bauteil1.D8
  N19: Display.B, Bauteil1.D3_PWM
  N20: R3.Pin_1, Bauteil1.A4/SDA
  N21: R4.Pin_1, Bauteil1.A3
  N22: R5.Pin_1, Bauteil1.A1
  N23: R6.Pin_1, Bauteil1.A2
